// Logisim project practica3.circ as structural Verilog
module EJERCICIO_2__SI_SOLO_SI (
  input  P,
  input  Q,
  output RESULTADO
);

  wire and_1_out, and_2_out, not_1_out, not_2_out;

  not not_1 (not_1_out, P);
  not not_2 (not_2_out, Q);
  and and_1 (and_1_out, not_1_out, not_2_out);
  and and_2 (and_2_out, P, Q);
  or or_1 (RESULTADO, and_1_out, and_2_out);

  // Notes on the sheet:
  //   SI SOLO SI
endmodule

module EJERCICIO_1_IMPLICACION (
  input  P,
  input  Q,
  output out_3
);

  wire transistor_1_out;

  Transistor transistor_1 (.in(1'b1), .out(transistor_1_out), .gate(P));
  Transistor #(.\type ("n")) transistor_2 (.in(1'b0), .out(transistor_1_out), .gate(P));
  Transistor transistor_3 (.in(Q), .out(out_3), .gate(transistor_1_out));
  Transistor #(.\type ("n")) transistor_4 (.in(1'b1), .out(out_3), .gate(transistor_1_out));

  // Notes on the sheet:
  //   IMPLICACION
endmodule

module EJERCICIO_3_COMPARADOR (
  input  y_0,
  input  y_1,
  input  x_1,
  input  x_0,
  output x____y
);

  wire and_1_out, and_2_out, and_3_out, and_4_out, and_5_out, not_1_out, not_2_out, not_3_out, not_4_out,
       not_5_out;

  not not_1 (not_1_out, y_0);
  not not_2 (not_2_out, y_1);
  not not_3 (not_3_out, y_0);
  not not_4 (not_4_out, y_0);
  not not_5 (not_5_out, y_1);
  and and_1 (and_1_out, not_1_out, not_2_out);
  and and_2 (and_2_out, x_0, not_3_out);
  and and_3 (and_3_out, x_1, not_4_out);
  and and_4 (and_4_out, x_0, x_1);
  and and_5 (and_5_out, x_0, not_5_out);
  or or_1 (x____y, and_1_out, and_2_out, and_3_out, and_4_out, and_5_out);

  // Notes on the sheet:
  //   X
  //   Y
  //   COMPARADOR
endmodule
