// Logisim project practica4.circ as structural Verilog: 2 circuits, main circuit main
module main (
  input  in_1,
  input  in_2,
  input  in_3
);

  wire sumador_completo_1_bit_1_sum;

  SUMADOR_COMPLETO_1_BIT sumador_completo_1_bit_1 (
    .A(in_1), .B(in_2), .Carry_In(in_3), .Sum(sumador_completo_1_bit_1_sum));  // open: Carry_Out
endmodule

module SUMADOR_COMPLETO_1_BIT (
  input  A,
  input  B,
  input  Carry_In,
  output Sum,
  output Carry_Out
);

  wire and_1_out, and_2_out, xor_1_out;

  xor xor_1 (xor_1_out, A, B);
  xor xor_2 (Sum, xor_1_out, Carry_In);
  and and_1 (and_1_out, xor_1_out, Carry_In);
  and and_2 (and_2_out, A, B);
  or or_1 (Carry_Out, and_1_out, and_2_out);
endmodule
